# Fritzing sketch esquematico (saved by Fritzing 0.9.3b)
breadboards: 1

parts:
  Arduino_Mega = Arduino Mega 2560 (Rev3)
  Mil = 7-SEGMENT-DISPLAY [package=7-segment-display]
  Centena = 7-SEGMENT-DISPLAY [package=7-segment-display]
  Decena = 7-SEGMENT-DISPLAY [package=7-segment-display]
  Unidad = 7-SEGMENT-DISPLAY [package=7-segment-display]
  DHT11 = DHT11 Humitidy and Temperature Sensor
  Componente1 = Adafruit DS3231 [part_number="Adafruit #3013"]
  HC-05 = Bluetooth HC-05 Macho
  Q1 = NPN-Transistor [package="TO92 [THT]"]
  Q2 = NPN-Transistor [package="TO92 [THT]"]
  Q3 = NPN-Transistor [package="TO92 [THT]"]
  Q4 = NPN-Transistor [package="TO92 [THT]"]
  R1 = Resistor [tolerance=±5% resistance=220 package=THT]
  R2 = Resistor [tolerance=±5% resistance=220 package=THT]
  R3 = Resistor [tolerance=±5% resistance=220 package=THT]
  R4 = Resistor [tolerance=±5% resistance=220 package=THT]

nets:
  N1: Arduino_Mega.D21/SCL, Componente1.SCL
  N2: Arduino_Mega.D20/SDA, Componente1.SDA
  N3: Arduino_Mega.D12_PWM, Decena.E
  N4: Arduino_Mega.D11_PWM, Decena.G
  N5: Arduino_Mega.D10_PWM, Decena.D
  N6: Arduino_Mega.D9_PWM, Decena.G1
  N7: Arduino_Mega.D8_PWM, Decena.DP
  5V: Arduino_Mega.5V, DHT11.VDD, Componente1.BAT, HC-05.VCC
  GND: Arduino_Mega.GND, DHT11.GND, Componente1.GND, HC-05.GND, Q1.C, Q2.C, Q3.C, Q4.C
  N8: Arduino_Mega.D2_PWM, R2.Pin_1
  N9: Arduino_Mega.D3_PWM, R1.Pin_1
  N10: Arduino_Mega.D4_PWM, R3.Pin_1
  N11: Arduino_Mega.D5_PWM, R4.Pin_1
  N12: Arduino_Mega.D6_PWM, Decena.G2
  N13: Arduino_Mega.D7_PWM, Decena.A
  N14: Arduino_Mega.D24, HC-05.TXD
  N15: Arduino_Mega.D25, HC-05.RXD
  N16: Arduino_Mega.D41, DHT11.DATA
  N17: Mil.F, Q4.E
  N18: Centena.F, Q3.E
  N19: Decena.C, Q1.E
  N20: Unidad.C, Q2.E
  N21: Q1.B, R3.Pin_0
  N22: Q2.B, R4.Pin_0
  N23: Q3.B, R1.Pin_0
  N24: Q4.B, R2.Pin_0

notes:
  SCL > 21
  SDA > 20
  DHT11
  DATA > 41 PIN
  --------Display 7 seg-----
  Unidad > 5 PIN
  Decena > 4 PIN
  Centena > 3 PIN
  Mil > 2 PIN
  ---------Display 7 seg--------
  a > 6 PIN b > 7 PIN c > 8 PIN d > 9 PIN
  e > 10 PIN f > 11PIN
  g > 12 PIN
  HC-05
  TXD > 24 PIN
  RXD > 23 PIN

custom parts:
  DHT11 Humitidy and Temperature Sensor: DHT11 Humidity and Temperature Sensor
  Adafruit DS3231: The datasheet for the DS3231 explains that this part is an "Extremely Accurate I²C-Integrated RTC/TCXO/Crystal". And, hey, it does exactly what it says on the tin! This Real Time Clock (RTC) is the most precise you can get in a small, low power package. Most RTCs use an external 32kHz timing crystal that is used to keep time with low current draw. And that's all well and good, but those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
